// Logisim project Traffic_Control_System_Project_Combinational_Circuit.circ as structural Verilog: 1 circuit, main circuit main
module main (
);

  wire CLK_out, Flip_Flop_1_q, Flip_Flop_1_qn, Flip_Flop_2_q, Flip_Flop_2_qn, Gate_0_out;

  Clock CLK (.out(CLK_out));
  D_Flip_Flop Flip_Flop_1 (
    .clk(CLK_out), .D(Flip_Flop_1_qn), .Q(Flip_Flop_1_q), .Qn(Flip_Flop_1_qn));  // open: preset, en, reset
  D_Flip_Flop Flip_Flop_2 (
    .clk(Flip_Flop_1_qn), .D(Flip_Flop_2_qn), .Q(Flip_Flop_2_q), .Qn(Flip_Flop_2_qn));  // open: preset, en, reset
  LED RED (.in(Flip_Flop_2_qn));
  LED YELLOW (.in(Flip_Flop_1_q));
  LED GREEN (.in(Gate_0_out));
  and Gate_0 (Gate_0_out, Flip_Flop_1_qn, Flip_Flop_2_q);

  // Notes on the sheet:
  //   Clock
  //   Red
  //   Yellow
  //   Green
  //   Pulse Waveform
  //   Traffic Control System
endmodule
