// Logisim project Traffic_Control_System_Project_Sequential_Circuit.circ as structural Verilog: 1 circuit, main circuit main
module main (
  input  in_1
);

  wire CLK_out, Flip_Flop_1_q, Flip_Flop_2_q, Flip_Flop_3_q, Flip_Flop_3_qn, Flip_Flop_4_q, Flip_Flop_4_qn,
       Gate_1_out, Gate_2_out, not_1_out, not_2_out;

  Clock CLK (.out(CLK_out));
  not not_1 (not_1_out, in_1);
  J_K_Flip_Flop Flip_Flop_1 (
    .J(not_1_out), .clk(CLK_out), .K(not_1_out), .Q(Flip_Flop_1_q));  // open: Qn, preset, en, reset
  not not_2 (not_2_out, Flip_Flop_1_q);
  J_K_Flip_Flop Flip_Flop_2 (
    .J(not_1_out), .clk(not_2_out), .K(not_1_out), .Q(Flip_Flop_2_q));  // open: Qn, preset, en, reset
  and Gate_1 (Gate_1_out, Flip_Flop_1_q, Flip_Flop_2_q);
  D_Flip_Flop Flip_Flop_3 (
    .clk(CLK_out), .D(Gate_1_out), .Q(Flip_Flop_3_q), .Qn(Flip_Flop_3_qn));  // open: preset, en, reset
  D_Flip_Flop Flip_Flop_4 (
    .clk(Flip_Flop_3_qn), .D(Flip_Flop_4_qn), .Q(Flip_Flop_4_q), .Qn(Flip_Flop_4_qn));  // open: preset, en, reset
  LED RED (.in(Flip_Flop_4_qn));
  LED YELLOW (.in(Flip_Flop_3_q));
  and Gate_2 (Gate_2_out, Flip_Flop_3_qn, Flip_Flop_4_q);
  LED GREEN (.in(Gate_2_out));

  // Notes on the sheet:
  //   Clock
  //   Red
  //   Yellow
  //   Green
  //   Pulse Waveforms
  //   Traffic Control System
endmodule
